// Logisim project 8_Bit_CPU.circ as structural Verilog: 1 circuit, main circuit main
module main (
  input  WRITE_EN,
  input  in_2,
  input  in_3,
  input  in_4,
  input  in_5,
  input  in_6,
  input  in_7,
  input  in_8,
  input  ADD_SUB,
  input  in_10,
  input  in_11,
  input  in_12,
  input  CTRL_SIGNAL_IN,
  input  CLOCK_IN,
  input  LSB_TO_BUS,
  input  LSB_FROM_BUS,
  input  in_17,
  input  in_18,
  input  in_19,
  input  in_20,
  input  in_21,
  input  in_22,
  input  in_23,
  input  in_24,
  input  in_25,
  input  in_26,
  input  in_27,
  input  in_28,
  input  TOGGLER_DIP_OR_REG,
  input  in_30,
  input  in_31,
  output [7:0] out_32
);

  wire ADD_IN_sw1, ADD_IN_sw2, ADD_IN_sw3, ADD_IN_sw4, clock_1_out, n74157_1_pin2, n74157_1_pin3,
       n74157_1_pin5, n74157_1_pin6, n74157_1_pin10, n74157_1_pin11, n74157_1_pin13, n74157_1_pin14,
       n74157_1_pin15, n74157_2_pin2, n74157_2_pin3, n74157_2_pin5, n74157_2_pin6, n74157_2_pin10,
       n74157_2_pin11, n74157_2_pin13, n74157_2_pin14, n74157_3_pin3, n74157_3_pin6, n74157_3_pin10,
       n74157_3_pin13, n74157_3_pin15, n74157_4_pin3, n74157_4_pin4, n74157_4_pin15, n74241_1_pin15,
       n74241_1_pin16, n74241_1_pin17, n74241_1_pin18, n74241_2_pin15, n74241_2_pin16, n74241_2_pin17,
       n74241_2_pin18, n74241_6_pin12, n74241_6_pin14, n74241_6_pin16, n74241_6_pin18, n74241_7_pin2,
       n74241_7_pin4, n74241_7_pin6, n74241_7_pin8, n74241_8_pin2, n74241_8_pin4, n74241_8_pin6,
       n74241_8_pin8, n74241_9_pin2, n74241_9_pin4, n74241_9_pin6, n74241_9_pin8, n74241_10_pin2,
       n74241_10_pin4, n74241_10_pin6, n74241_10_pin8, n74241_11_pin12, n74241_11_pin14, n74241_11_pin16,
       n74241_12_pin12, n74241_12_pin14, n74241_12_pin16, n74241_12_pin18, n74283_1_pin2, n74283_1_pin6,
       n74283_1_pin9, n74283_1_pin11, n74283_1_pin15, n74283_2_pin2, n74283_2_pin6, n74283_2_pin11,
       n74283_2_pin15, not_1_out, RA1, RA2, RA3, RA4, RA5, RA6, RA7, RA8, RB1, RB2, RB3, RB4, RB5, RB6, RB7,
       RB8;
  wire [1:0] n74157_2_pin4, n74157_2_pin9, n74157_3_pin4, n74157_3_pin9, n74241_2_pin5, n74241_2_pin9,
       n74241_4_pin5, n74241_4_pin9, n74241_6_pin5, n74241_6_pin9;
  wire [3:0] n74157_1_pin4, n74241_1_pin9, n74241_3_pin9, n74241_5_pin9;
  wire [7:0] register_3_q;

  Clock clock_1 (.out(clock_1_out));
  Register register_1 (
    .D({n74241_2_pin5, n74241_2_pin9, n74241_1_pin9}), .en(WRITE_EN), .clk(clock_1_out),
    .Q({RA8, RA7, RA6, RA5, RA4, RA3, RA2, RA1}), .clr(in_4));
  Register register_2 (
    .D({n74241_4_pin5, n74241_4_pin9, n74241_3_pin9}), .en(in_5), .clk(clock_1_out),
    .Q({RB8, RB7, RB6, RB5, RB4, RB3, RB2, RB1}), .clr(in_7));
  Register register_3 (
    .D({n74241_6_pin5, n74241_6_pin9, n74241_5_pin9}), .en(in_10), .clk(clock_1_out), .Q(register_3_q),
    .clr(in_12));
  _74241 u_74241_1 (
    .pin1(in_2), .pin2(RA1), .pin3(n74241_1_pin9[3]), .pin4(RA2), .pin5(n74241_1_pin9[2]), .pin6(RA3),
    .pin7(n74241_1_pin9[1]), .pin8(RA4), .pin9(n74241_1_pin9[0]), .pin19(WRITE_EN), .pin18(n74241_1_pin18),
    .pin17(n74241_1_pin17), .pin16(n74241_1_pin16), .pin15(n74241_1_pin15), .pin14(n74241_1_pin15),
    .pin13(n74241_1_pin16), .pin12(n74241_1_pin17), .pin11(n74241_1_pin18));
  _74241 u_74241_2 (
    .pin1(in_2), .pin2(RA5), .pin3(n74241_2_pin5[1]), .pin4(RA6), .pin5(n74241_2_pin5[0]), .pin6(RA7),
    .pin7(n74241_2_pin9[1]), .pin8(RA8), .pin9(n74241_2_pin9[0]), .pin19(WRITE_EN), .pin18(n74241_2_pin18),
    .pin17(n74241_2_pin17), .pin16(n74241_2_pin16), .pin15(n74241_2_pin15), .pin14(n74241_2_pin15),
    .pin13(n74241_2_pin16), .pin12(n74241_2_pin17), .pin11(n74241_2_pin18));
  _74241 u_74241_3 (
    .pin1(in_6), .pin2(RB1), .pin3(n74241_3_pin9[3]), .pin4(RB2), .pin5(n74241_3_pin9[2]), .pin6(RB3),
    .pin7(n74241_3_pin9[1]), .pin8(RB4), .pin9(n74241_3_pin9[0]), .pin19(in_5), .pin18(n74241_1_pin18),
    .pin17(n74241_1_pin17), .pin16(n74241_1_pin16), .pin15(n74241_1_pin15), .pin14(n74241_1_pin15),
    .pin13(n74241_1_pin16), .pin12(n74241_1_pin17), .pin11(n74241_1_pin18));
  _74241 u_74241_4 (
    .pin1(in_6), .pin2(RB5), .pin3(n74241_4_pin5[1]), .pin4(RB6), .pin5(n74241_4_pin5[0]), .pin6(RB7),
    .pin7(n74241_4_pin9[1]), .pin8(RB8), .pin9(n74241_4_pin9[0]), .pin19(in_5), .pin18(n74241_2_pin18),
    .pin17(n74241_2_pin17), .pin16(n74241_2_pin16), .pin15(n74241_2_pin15), .pin14(n74241_2_pin15),
    .pin13(n74241_2_pin16), .pin12(n74241_2_pin17), .pin11(n74241_2_pin18));
  _74241 u_74241_5 (
    .pin1(in_11), .pin2(register_3_q[0]), .pin3(n74241_5_pin9[3]), .pin4(register_3_q[1]),
    .pin5(n74241_5_pin9[2]), .pin6(register_3_q[2]), .pin7(n74241_5_pin9[1]), .pin8(register_3_q[3]),
    .pin9(n74241_5_pin9[0]), .pin19(in_10), .pin18(n74241_1_pin18), .pin17(n74241_1_pin17),
    .pin16(n74241_1_pin16), .pin15(n74241_1_pin15), .pin14(n74241_1_pin15), .pin13(n74241_1_pin16),
    .pin12(n74241_1_pin17), .pin11(n74241_1_pin18));
  _74241 u_74241_6 (
    .pin1(in_11), .pin2(register_3_q[4]), .pin3(n74241_6_pin5[1]), .pin4(register_3_q[5]),
    .pin5(n74241_6_pin5[0]), .pin6(register_3_q[6]), .pin7(n74241_6_pin9[1]), .pin8(register_3_q[7]),
    .pin9(n74241_6_pin9[0]), .pin19(in_10), .pin18(n74241_6_pin18), .pin17(n74241_2_pin17),
    .pin16(n74241_6_pin16), .pin15(n74241_2_pin15), .pin14(n74241_6_pin14), .pin13(n74241_2_pin16),
    .pin12(n74241_6_pin12), .pin11(n74241_2_pin18));
  // _74377 74377_1: pin names not known; wires that end beside it: 1'b1, 1'b0
  // _74377 74377_2: pin names not known; wires that end beside it: 1'b1, 1'b0
  // _74377 74377_3: pin names not known; wires that end beside it: 1'b1, 1'b0
  // _74377 74377_4: pin names not known; wires that end beside it: 1'b1, 1'b0
  // _74377 74377_5: pin names not known; wires that end beside it: 1'b1, 1'b0
  // _74377 74377_6: pin names not known; wires that end beside it: 1'b1, 1'b0
  // _74377 74377_7: pin names not known; wires that end beside it: 1'b1, 1'b0
  // _74377 74377_8: pin names not known; wires that end beside it: 1'b1, 1'b0
  // _74377 74377_9: pin names not known; wires that end beside it: 1'b1, 1'b0
  // _74377 74377_10: pin names not known; wires that end beside it: 1'b1, 1'b0
  // _74377 74377_11: pin names not known; wires that end beside it: 1'b1, 1'b0
  // _74377 74377_12: pin names not known; wires that end beside it: 1'b1, 1'b0
  // _74377 74377_13: pin names not known; wires that end beside it: 1'b1, 1'b0
  // _74377 74377_14: pin names not known; wires that end beside it: 1'b1, 1'b0
  // _74377 74377_15: pin names not known; wires that end beside it: 1'b1, 1'b0
  // _74377 74377_16: pin names not known; wires that end beside it: 1'b1, 1'b0
  LED led_1 (.in(n74241_6_pin12));
  LED led_2 (.in(n74241_6_pin14));
  LED led_3 (.in(n74241_6_pin16));
  LED led_4 (.in(n74241_6_pin18));
  LED led_5 (.in(n74241_1_pin17));
  LED led_6 (.in(n74241_1_pin15));
  LED led_7 (.in(n74241_1_pin16));
  LED led_8 (.in(n74241_1_pin18));
  LED LSB_BUS (.in(n74241_1_pin18));
  LED led_9 (.in(n74241_1_pin16));
  LED led_10 (.in(n74241_1_pin15));
  LED led_11 (.in(n74241_1_pin17));
  LED led_12 (.in(n74241_2_pin18));
  LED led_13 (.in(n74241_2_pin16));
  LED led_14 (.in(n74241_2_pin15));
  LED MSB_BUS (.in(n74241_2_pin17));
  _74241 u_74241_7 (
    .pin1(in_3), .pin2(n74241_7_pin2), .pin4(n74241_7_pin4), .pin6(n74241_7_pin6), .pin8(n74241_7_pin8),
    .pin18(n74241_1_pin18), .pin16(n74241_1_pin16), .pin14(n74241_1_pin15), .pin12(n74241_1_pin17));  // open: pin3, pin5, pin7, pin9, pin19, pin17, pin15, pin13, pin11
  _74241 u_74241_8 (
    .pin1(in_3), .pin2(n74241_8_pin2), .pin4(n74241_8_pin4), .pin6(n74241_8_pin6), .pin8(n74241_8_pin8),
    .pin18(n74241_2_pin18), .pin16(n74241_2_pin16), .pin14(n74241_2_pin15), .pin12(n74241_2_pin17));  // open: pin3, pin5, pin7, pin9, pin19, pin17, pin15, pin13, pin11
  DipSwitch dipswitch_1 (
    .sw1(n74241_7_pin2), .sw2(n74241_7_pin4), .sw3(n74241_7_pin6), .sw4(n74241_7_pin8), .sw5(n74241_8_pin2),
    .sw6(n74241_8_pin4), .sw7(n74241_8_pin6), .sw8(n74241_8_pin8));
  _74157 u_74157_1 (
    .pin1(TOGGLER_DIP_OR_REG), .pin2(n74157_1_pin2), .pin3(n74157_1_pin3), .pin4(n74157_1_pin4[0]),
    .pin5(n74157_1_pin5), .pin6(n74157_1_pin6), .pin7(n74157_1_pin4[1]), .pin15(n74157_1_pin15),
    .pin14(n74157_1_pin14), .pin13(n74157_1_pin13), .pin12(n74157_1_pin4[3]), .pin11(n74157_1_pin11),
    .pin10(n74157_1_pin10), .pin9(n74157_1_pin4[2]));
  _74157 u_74157_2 (
    .pin1(TOGGLER_DIP_OR_REG), .pin2(n74157_2_pin2), .pin3(n74157_2_pin3), .pin4(n74157_2_pin4[0]),
    .pin5(n74157_2_pin5), .pin6(n74157_2_pin6), .pin7(n74157_2_pin4[1]), .pin15(n74157_1_pin15),
    .pin14(n74157_2_pin14), .pin13(n74157_2_pin13), .pin12(n74157_2_pin9[1]), .pin11(n74157_2_pin11),
    .pin10(n74157_2_pin10), .pin9(n74157_2_pin9[0]));
  DipSwitch DATA_IN (
    .sw1(n74157_1_pin2), .sw2(n74157_1_pin5), .sw3(n74157_1_pin11), .sw4(n74157_1_pin14),
    .sw5(n74157_2_pin2), .sw6(n74157_2_pin5), .sw7(n74157_2_pin11), .sw8(n74157_2_pin14));
  LED LSB (.in(n74241_1_pin18));
  LED led_15 (.in(n74241_1_pin16));
  LED led_16 (.in(n74241_1_pin15));
  LED led_17 (.in(n74241_1_pin17));
  LED led_18 (.in(n74241_2_pin18));
  LED led_19 (.in(n74241_2_pin16));
  LED led_20 (.in(n74241_2_pin15));
  LED MSB (.in(n74241_2_pin17));
  DipSwitch #(.number(4)) ADD_IN (.sw1(ADD_IN_sw1), .sw2(ADD_IN_sw2), .sw3(ADD_IN_sw3), .sw4(ADD_IN_sw4));
  _74241 u_74241_9 (
    .pin1(in_8), .pin2(n74241_9_pin2), .pin4(n74241_9_pin4), .pin6(n74241_9_pin6), .pin8(n74241_9_pin8),
    .pin18(n74241_1_pin18), .pin16(n74241_1_pin16), .pin14(n74241_1_pin15), .pin12(n74241_1_pin17));  // open: pin3, pin5, pin7, pin9, pin19, pin17, pin15, pin13, pin11
  _74241 u_74241_10 (
    .pin1(in_8), .pin2(n74241_10_pin2), .pin4(n74241_10_pin4), .pin6(n74241_10_pin6), .pin8(n74241_10_pin8),
    .pin18(n74241_2_pin18), .pin16(n74241_2_pin16), .pin14(n74241_2_pin15), .pin12(n74241_2_pin17));  // open: pin3, pin5, pin7, pin9, pin19, pin17, pin15, pin13, pin11
  _74283 u_74283_1 (
    .pin1(n74241_9_pin4), .pin2(n74283_1_pin2), .pin3(RA2), .pin4(n74241_9_pin2), .pin5(RA1),
    .pin6(n74283_1_pin6), .pin7(ADD_SUB), .pin15(n74283_1_pin15), .pin14(RA3), .pin13(n74241_9_pin6),
    .pin12(RA4), .pin11(n74283_1_pin11), .pin10(n74241_9_pin8), .pin9(n74283_1_pin9));
  xor xor_1 (n74283_1_pin6, RB1, ADD_SUB);
  not not_1 (not_1_out, in_17);
  _74157 u_74157_3 (
    .pin1(TOGGLER_DIP_OR_REG), .pin2(ADD_IN_sw1), .pin3(n74157_3_pin3), .pin4(n74157_3_pin4[0]),
    .pin5(ADD_IN_sw2), .pin6(n74157_3_pin6), .pin7(n74157_3_pin4[1]), .pin15(n74157_3_pin15),
    .pin14(ADD_IN_sw4), .pin13(n74157_3_pin13), .pin12(n74157_3_pin9[1]), .pin11(ADD_IN_sw3),
    .pin10(n74157_3_pin10), .pin9(n74157_3_pin9[0]));
  xor xor_2 (n74283_1_pin2, RB2, ADD_SUB);
  xor xor_3 (n74283_1_pin15, RB3, ADD_SUB);
  _74157 u_74157_4 (
    .pin1(not_1_out), .pin2(in_17), .pin3(n74157_4_pin3), .pin4(n74157_4_pin4), .pin15(n74157_4_pin15));  // open: pin5, pin6, pin7, pin14, pin13, pin12, pin11, pin10, pin9
  xor xor_4 (n74283_1_pin11, RB4, ADD_SUB);
  _74283 u_74283_2 (
    .pin1(n74241_10_pin4), .pin2(n74283_2_pin2), .pin3(RA6), .pin4(n74241_10_pin2), .pin5(RA5),
    .pin6(n74283_2_pin6), .pin7(n74283_1_pin9), .pin15(n74283_2_pin15), .pin14(RA7), .pin13(n74241_10_pin6),
    .pin12(RA8), .pin11(n74283_2_pin11), .pin10(n74241_10_pin8));  // open: pin9
  xor xor_5 (n74283_2_pin6, RB5, ADD_SUB);
  LED LSB_ADR_REG (.in(n74157_3_pin4[0]));
  LED led_21 (.in(n74157_3_pin4[1]));
  LED led_22 (.in(n74157_3_pin9[0]));
  LED MSB_ADR_REG (.in(n74157_3_pin9[1]));
  _74175 u_74175_1 (
    .pin1(in_28), .pin2(n74157_3_pin3), .pin7(n74157_3_pin6), .pin15(n74157_3_pin13), .pin13(in_23),
    .pin12(in_20), .pin10(n74157_3_pin10), .pin9(in_26));  // open: pin3, pin4, pin5, pin6, pin14, pin11
  xor xor_6 (n74283_2_pin2, RB6, ADD_SUB);
  xor xor_7 (n74283_2_pin15, RB7, ADD_SUB);
  and and_1 (n74157_4_pin3, CTRL_SIGNAL_IN, CLOCK_IN);
  xor xor_8 (n74283_2_pin11, RB8, ADD_SUB);
  RAM ram_1 (
    .addr({in_24, in_22, in_21, in_19, n74157_3_pin9, n74157_3_pin4}), .we(n74157_4_pin4), .oe(in_25),
    .clk(in_27), .din({n74157_2_pin9, n74157_2_pin4, n74157_1_pin4}), .dout(out_32));
  _74241 u_74241_11 (
    .pin1(in_18), .pin2(out_32[0]), .pin4(out_32[1]), .pin6(out_32[2]), .pin8(out_32[3]),
    .pin18(n74157_1_pin3), .pin16(n74241_11_pin16), .pin14(n74241_11_pin14), .pin12(n74241_11_pin12));  // open: pin3, pin5, pin7, pin9, pin19, pin17, pin15, pin13, pin11
  _74241 u_74241_12 (
    .pin1(in_18), .pin2(out_32[4]), .pin4(out_32[5]), .pin6(out_32[6]), .pin8(out_32[7]),
    .pin18(n74241_12_pin18), .pin16(n74241_12_pin16), .pin14(n74241_12_pin14), .pin12(n74241_12_pin12));  // open: pin3, pin5, pin7, pin9, pin19, pin17, pin15, pin13, pin11
  // also tied to GND on the sheet: {n74157_1_pin15, n74157_3_pin15, n74157_4_pin15}

  // Other names for the same wires on the sheet: A = in_2; A1 = in_6; A3 = in_11; B = WRITE_EN; B1 = in_5; B3 = in_10

  // Notes on the sheet:
  //   REG B
  //   REG A
  //   ALU
  //   RAM DIVISION
  //   ADDRESS_REG
endmodule
